// Logisim project control-logic.circ as structural Verilog: 1 circuit, main circuit control_logic
module control_logic (
  input  [31:0] Instruction,
  input  BrEq,
  input  BrLt,
  output PCSel,
  output RegWEn,
  output [2:0] ImmSel,
  output BrUn,
  output ASel,
  output BSel,
  output [3:0] ALUSel,
  output MemWEn,
  output [1:0] WBSel
);

  wire and_7_out, and_10_out, and_11_out, and_18_out, and_19_out, and_20_out, and_21_out, and_22_out,
       and_23_out, and_24_out, and_25_out, and_26_out, and_27_out, and_28_out, and_29_out, and_30_out,
       and_31_out, and_32_out, and_33_out, comparator_5_eq, comparator_6_eq, comparator_9_eq,
       comparator_10_eq, funct3_0b000, funct3_0b001, funct3_0b010, funct3_0b011, funct3_0b100, funct3_0b101,
       funct3_0b110, funct3_0b111, funct7_0b0000000, funct7_0b0000001, funct7_0b0100000, is_add, is_addi,
       is_and, is_andi, is_beq, is_bge, is_bgeu, is_blt, is_bltu, is_bne, is_mul, is_mulh, is_mulhu, is_or,
       is_ori, is_sll, is_slli, is_slt, is_slti, is_sra, is_srai, is_srl, is_srli, is_sub, is_xor, is_xori,
       not_1_out, not_2_out, or_4_out, or_5_out, or_6_out, typeB, typeI, typeJ, typeL, typeR, typeS, typeU;
  wire [5:0] RomInput;
  wire [15:14] rom_1_data;

  Demultiplexer #(.select(3)) demultiplexer_1 (
    .out0(funct3_0b000), .out1(funct3_0b001), .out2(funct3_0b010), .out3(funct3_0b011), .out4(funct3_0b100),
    .out5(funct3_0b101), .out6(funct3_0b110), .out7(funct3_0b111), .in(1'b1), .sel(Instruction[14:12]));
  Comparator #(.width(7)) comparator_1 (.a(Instruction[31:25]), .b({7{1'b0}}), .eq(funct7_0b0000000));  // open: gt, lt
  Comparator #(.width(7)) comparator_2 (.a(Instruction[31:25]), .b(7'b0000001), .eq(funct7_0b0000001));  // open: gt, lt
  Comparator #(.width(7)) comparator_3 (.a(Instruction[31:25]), .b(7'b0100000), .eq(funct7_0b0100000));  // open: gt, lt
  and and_1 (is_beq, funct3_0b000, typeB);
  and and_2 (is_bne, funct3_0b001, typeB);
  and and_3 (is_blt, funct3_0b100, typeB);
  and and_4 (is_bge, funct3_0b101, typeB);
  and and_5 (is_bltu, funct3_0b110, typeB);
  and and_6 (is_bgeu, funct3_0b111, typeB);
  ROM #(.addrWidth(6), .dataWidth(16)) rom_1 (
    .addr(RomInput), .data({rom_1_data, WBSel, MemWEn, ALUSel, BSel, ASel, BrUn, ImmSel, RegWEn}));
  and and_7 (and_7_out, funct3_0b001, funct7_0b0000000);
  and and_8 (is_slti, funct3_0b010, typeI);
  and and_9 (is_xori, funct3_0b100, typeI);
  and and_10 (and_10_out, funct3_0b101, funct7_0b0000000);
  and and_11 (and_11_out, funct3_0b101, funct7_0b0100000);
  and and_12 (is_ori, funct3_0b110, typeI);
  and and_13 (is_andi, funct3_0b111, typeI);
  and and_14 (is_addi, funct3_0b000, typeI);
  Comparator #(.width(7)) comparator_4 (.a(7'b0110011), .b(Instruction[6:0]), .eq(typeR));  // open: gt, lt
  Comparator #(.width(7)) comparator_5 (.a(7'b0000011), .b(Instruction[6:0]), .eq(comparator_5_eq));  // open: gt, lt
  Comparator #(.width(7)) comparator_6 (.a(7'b0010011), .b(Instruction[6:0]), .eq(comparator_6_eq));  // open: gt, lt
  Comparator #(.width(7)) comparator_7 (.a(7'b0100011), .b(Instruction[6:0]), .eq(typeS));  // open: gt, lt
  Comparator #(.width(7)) comparator_8 (.a(7'b1100011), .b(Instruction[6:0]), .eq(typeB));  // open: gt, lt
  Comparator #(.width(7)) comparator_9 (.a(7'b0010111), .b(Instruction[6:0]), .eq(comparator_9_eq));  // open: gt, lt
  Comparator #(.width(7)) comparator_10 (.a(7'b0110111), .b(Instruction[6:0]), .eq(comparator_10_eq));  // open: gt, lt
  Comparator #(.width(7)) comparator_11 (.a(7'b1101111), .b(Instruction[6:0]), .eq(typeJ));  // open: gt, lt
  Comparator #(.width(7)) comparator_12 (.a(7'b1100111), .b(Instruction[6:0]), .eq(typeL));  // open: gt, lt
  and and_15 (is_slli, and_7_out, typeI);
  and and_16 (is_srli, and_10_out, typeI);
  and and_17 (is_srai, and_11_out, typeI);
  or or_1 (typeI, comparator_5_eq, comparator_6_eq);
  or or_2 (typeU, comparator_9_eq, comparator_10_eq);
  or or_3 (PCSel, and_18_out, and_20_out, and_21_out, and_19_out);
  and and_18 (and_18_out, is_beq, BrEq);
  and and_19 (and_19_out, is_bne, not_1_out);
  and and_20 (and_20_out, or_4_out, or_5_out);
  and and_21 (and_21_out, or_6_out, BrLt);
  not not_1 (not_1_out, BrEq);
  or or_4 (or_4_out, is_bge, is_bgeu);
  or or_5 (or_5_out, BrEq, not_2_out);
  or or_6 (or_6_out, is_blt, is_bltu);
  not not_2 (not_2_out, BrLt);
  and and_22 (and_22_out, funct3_0b000, funct7_0b0000000);
  and and_23 (and_23_out, funct3_0b000, funct7_0b0000001);
  and and_24 (and_24_out, funct3_0b000, funct7_0b0100000);
  and and_25 (and_25_out, funct3_0b001, funct7_0b0000000);
  and and_26 (and_26_out, funct3_0b001, funct7_0b0000001);
  and and_27 (and_27_out, funct3_0b011, funct7_0b0000001);
  and and_28 (and_28_out, funct3_0b010, funct7_0b0000000);
  and and_29 (and_29_out, funct3_0b100, funct7_0b0000000);
  and and_30 (and_30_out, funct3_0b101, funct7_0b0000000);
  and and_31 (and_31_out, funct3_0b101, funct7_0b0100000);
  and and_32 (and_32_out, funct3_0b110, funct7_0b0000000);
  and and_33 (and_33_out, funct3_0b111, funct7_0b0000000);
  and and_34 (is_add, and_22_out, typeR);
  and and_35 (is_mul, and_23_out, typeR);
  and and_36 (is_sub, and_24_out, typeR);
  and and_37 (is_sll, and_25_out, typeR);
  and and_38 (is_mulh, and_26_out, typeR);
  and and_39 (is_mulhu, and_27_out, typeR);
  and and_40 (is_slt, and_28_out, typeR);
  and and_41 (is_xor, and_29_out, typeR);
  and and_42 (is_srl, and_30_out, typeR);
  and and_43 (is_sra, and_31_out, typeR);
  and and_44 (is_or, and_32_out, typeR);
  and and_45 (is_and, and_33_out, typeR);
  Priority_Encoder #(.select_enc(6)) priority_encoder_1 (
    .in0(is_add), .in1(is_mul), .in2(is_sub), .in3(is_sll), .in4(is_mulh), .in5(is_mulhu), .in6(is_slt),
    .in7(is_xor), .in8(is_srl), .in9(is_sra), .in10(is_or), .in11(is_and), .in15(is_addi), .in16(is_slli),
    .in17(is_slti), .in18(is_xori), .in19(is_srli), .in20(is_srai), .in21(is_ori), .in22(is_andi),
    .in26(is_beq), .in27(is_bne), .in28(is_blt), .in29(is_bge), .in30(is_bltu), .in31(is_bgeu), .out(RomInput));  // open: in12, in13, in14, in23, in24, in25, in32, in33, in34, in35, in36, in37, in38, in39, in40, in41, in42, in43, in44, in45, in46, in47, in48, in49, in50, in51, in52, in53, in54, in55, in56, in57, in58, in59, in60, in61, in62, in63, gs, en_out, en_in

  // Other names for the same wires on the sheet: opcode[6:0] = Instruction[6:0]; funct3[2:0] = Instruction[14:12];
  //   funct7[6:0] = Instruction[31:25]

  // Notes on the sheet:
  //   INPUTS to your circuit
  //   contents of rom_1 (hex, n*v repeats v):
  //   1001 1401 1601 1081 1481 1581 1101 1201 1281 1681 1301 1381 0 0 0 1041 10c1 1141 1241 12c1 16c1 1341
  //   13c1 0 0 0 4*1064 1074 1074
  //   ROM FOR CONTROL LOGIC
  //   DON'T CHANGE THE LOCATIONS OF THE INPUTS AND OUTPUTS!
  //   This is only if you choose to do the ROM option
  //   OUTPUT from your circuit
  //   Reminder: If using ROM, use combinational logic for PCSel
endmodule
